# Fritzing sketch CapstoneSmartBagFritzing (saved by Fritzing 1.0.4)
breadboards: 1

parts:
  A1 = Particle - Photon2
  M1 = BMP280
  M2 = BMP280
  OLED_I2C1 = OLED 128x64 I2C Monochrome Display
  Water_Level_Sensor1 = Water Level Sensor
  Part1 = InvenSense MPU6050
  S1 = Round Pushbutton

nets:
  VIN: A1.Pin_2, A1.Pin_31, M1.VIN, M2.VIN, OLED_I2C1.VDD, Part1.VCC
  GND: A1.Pin_4, A1.Pin_35, M1.GND, M2.GND, OLED_I2C1.GND, Water_Level_Sensor1.GND, Part1.GND, S1.leg1
  N1: A1.Pin_17, M1.SDA, M2.SDA, OLED_I2C1.SDA, Part1.SDA
  N2: A1.Pin_18, M1.SCL, M2.SCL, OLED_I2C1.SCK, Part1.SCL
  N3: A1.Pin_22, Water_Level_Sensor1.SIG
  N4: A1.Pin_26, Water_Level_Sensor1.VCC
  N5: A1.Pin_27, S1.leg0

custom parts:
  Particle - Photon2: The Photon 2 is a microcontroller and Wi-Fi networking developed by particle. Features: 802.11a/b/g/n Wi-Fi, 2.4 GHz and 5 GHz Integrated PCB antenna Integrated U.FL connector for external antenna Integrated RF switch BLE 5 using same antenna as Wi-Fi Realtek RTL8721DM MCU ARM Cortex M33 CPU, 200 MHz 2048 KB (2 MB) user application maximum size 3072 KB (3 MB) of RAM available to user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
  BMP280: Temperature Humidity Barometric presure Sensor, I2C
  Water Level Sensor: A water level sensor. This sensor operates at 3V to 5V. The Sig (signal) pin outputs an analogue signal that is in proportion to the amount of water in contact with the sensor.
